# Fritzing sketch FFB_Arduino_Yoke_1.0_Leonardo (saved by Fritzing 0.9.3b)

parts:
  Bauteil1 = Arduino Leonardo (Rev3b)
  M1 = BTS7960
  M2 = BTS7960
  R1 = Rotary Potentiometer (Small) [maximum_resistance=100kΩ package=THT]
  R3 = Rotary Potentiometer (Small) [maximum_resistance=100kΩ package=THT]
  S3 = Pushbutton [package="[SMD]"]
  M4 = DC Motor
  M5 = DC Motor
  HLK-PM2 = HLK-PM12 [part_number=HLK-PM12]
  S10 = Pushbutton [package="[SMD]"]
  S11 = Pushbutton [package="[SMD]"]
  S12 = Pushbutton [package="[SMD]"]
  S13 = Pushbutton [package="[SMD]"]
  S14 = Pushbutton [package="[SMD]"]
  S15 = Pushbutton [package="[SMD]"]
  S16 = Pushbutton [package="[SMD]"]
  S17 = Pushbutton [package="[SMD]"]
  S18 = Pushbutton [package="[SMD]"]
  S25 = Limit Switch [package="Breakout Board"]
  S26 = Limit Switch [package="Breakout Board"]
  S27 = Limit Switch [package="Breakout Board"]
  S28 = Limit Switch [package="Breakout Board"]
  S29 = Pushbutton [package="[SMD]"]
  S30 = Pushbutton [package="[SMD]"]
  S31 = Pushbutton [package="[SMD]"]
  S32 = Pushbutton [package="[SMD]"]
  S33 = Pushbutton [package="[SMD]"]
  S34 = Pushbutton [package="[SMD]"]
  S35 = Pushbutton [package="[SMD]"]
  Bauteil3 = Analog Digital MUX Breakout
  Bauteil4 = Analog Digital MUX Breakout
  R29 = Rotary Potentiometer (Small) [maximum_resistance=10kΩ package=THT]
  R30 = Rotary Potentiometer (Small) [maximum_resistance=10kΩ package=THT]
  R31 = Rotary Potentiometer (Small) [maximum_resistance=10kΩ package=THT]
  R32 = Rotary Potentiometer (Small) [maximum_resistance=10kΩ package=THT]
  R33 = Rotary Potentiometer (Small) [maximum_resistance=10kΩ package=THT]
  R34 = Rotary Potentiometer (Small) [maximum_resistance=10kΩ package=THT]
  R42 = Resistor [tolerance=±5% resistance=10k package="0402 [SMD]"]
  R43 = Resistor [tolerance=±5% resistance=10k package="0402 [SMD]"]
  R44 = Resistor [tolerance=±5% resistance=10k package="0402 [SMD]"]
  R45 = Resistor [tolerance=±5% resistance=10k package="0402 [SMD]"]
  R46 = Resistor [tolerance=±5% resistance=10k package="0402 [SMD]"]
  R47 = Resistor [tolerance=±5% resistance=10k package="0402 [SMD]"]
  R48 = Resistor [tolerance=±5% resistance=10k package="0402 [SMD]"]
  R49 = Resistor [tolerance=±5% resistance=10k package="0402 [SMD]"]
  R50 = Resistor [tolerance=±5% resistance=10k package="0402 [SMD]"]
  R51 = Resistor [tolerance=±5% resistance=10k package="0402 [SMD]"]
  R52 = Resistor [tolerance=±5% resistance=10k package="0402 [SMD]"]
  R53 = Resistor [tolerance=±5% resistance=10k package="0402 [SMD]"]
  R54 = Resistor [tolerance=±5% resistance=10k package="0402 [SMD]"]
  R55 = Resistor [tolerance=±5% resistance=10k package="0402 [SMD]"]
  R56 = Resistor [tolerance=±5% resistance=10k package="0402 [SMD]"]
  R57 = Resistor [tolerance=±5% resistance=10k package="0402 [SMD]"]
  R58 = Resistor [tolerance=±5% resistance=10k package="0402 [SMD]"]
  R59 = Resistor [tolerance=±5% resistance=10k package="0402 [SMD]"]
  R60 = Resistor [tolerance=±5% resistance=10k package="0402 [SMD]"]
  R61 = Resistor [tolerance=±5% resistance=10k package="0402 [SMD]"]
  R62 = Resistor [tolerance=±5% resistance=10k package="0402 [SMD]"]
  U1 = 74HC595 [package="DIP16 [THT]"]
  LCD2004-I2C1 = LCD screen
  R63 = Rotary Potentiometer (Small) [maximum_resistance=10kΩ package=THT]
  R64 = Rotary Potentiometer (Small) [maximum_resistance=10kΩ package=THT]

nets:
  N1: Bauteil1.D0/RX, U1.ST_CP
  N2: Bauteil1.D1/TX, Bauteil4.EN
  N3: Bauteil1.D2/SDA, Bauteil1.SDA, Bauteil3.EN
  N4: Bauteil1.D3_PWM/SCL, Bauteil1.SCL, Bauteil3.S2, Bauteil4.S2
  N5: Bauteil1.D4/A6, Bauteil3.S0, Bauteil4.S0
  N6: Bauteil1.D5_PWM, Bauteil3.S1, Bauteil4.S1
  N7: Bauteil1.D6_PWM/A7, M1.pin1
  N8: Bauteil1.D7, Bauteil3.S3, Bauteil4.S3
  VCC: Bauteil1.5V, M1.pin7, M2.pin7, R1.leg1, R3.leg1, S3.Pin_1, S3.Pin_2, S10.Pin_1, S10.Pin_2, S11.Pin_1, S11.Pin_2, S12.Pin_1, S12.Pin_2, S13.Pin_1, S13.Pin_2, S14.Pin_1, S14.Pin_2, S15.Pin_1, S15.Pin_2, S16.Pin_1, S16.Pin_2, S17.Pin_1, S17.Pin_2, S18.Pin_1, S18.Pin_2, S25.S, S26.S, S27.S, S28.S, S29.Pin_1, S29.Pin_2, S30.Pin_1, S30.Pin_2, S31.Pin_1, S31.Pin_2, S32.Pin_1, S32.Pin_2, S33.Pin_1, S33.Pin_2, S34.Pin_1, S34.Pin_2, S35.Pin_1, S35.Pin_2, Bauteil3.VCC, Bauteil4.VCC, R29.leg2, R30.leg2, R31.leg2, R32.leg2, R33.leg2, R34.leg2, U1.MR, U1.VCC, LCD2004-I2C1.VSS
  GND: Bauteil1.GND, M1.pin8, M2.pin8, R1.leg2, R3.leg2, Bauteil3.GND, Bauteil4.GND, R29.leg1, R30.leg1, R31.leg1, R32.leg1, R33.leg1, R34.leg1, R42.Pin_1, R43.Pin_1, R44.Pin_1, R45.Pin_1, R46.Pin_1, R47.Pin_1, R48.Pin_1, R49.Pin_1, R50.Pin_1, R51.Pin_1, R52.Pin_1, R53.Pin_1, R54.Pin_1, R55.Pin_1, R56.Pin_1, R57.Pin_1, R58.Pin_1, R59.Pin_1, R60.Pin_1, R61.Pin_1, R62.Pin_1, U1.GND, U1.OE, LCD2004-I2C1.LED-
  N9: Bauteil1.A0, R3.wiper
  N10: Bauteil1.A1, R1.wiper
  N11: Bauteil1.A3, U1.DS
  N12: Bauteil1.A4, Bauteil4.SIG
  N13: Bauteil1.A5, Bauteil3.SIG
  N14: Bauteil1.D8/A8, M2.pin3, M2.pin4
  N15: Bauteil1.D9_PWM/A9, M2.pin1
  N16: Bauteil1.D10_PWM/A10, M2.pin2
  N17: Bauteil1.D11_PWM, M1.pin3, M1.pin4
  N18: Bauteil1.D12/A11, U1.SH_CP
  N19: Bauteil1.D13_PWM, M1.pin2
  N20: M1.pin9, M4.pin_2
  N21: M1.pin10, M4.pin_1
  N22: M1.pin11, M2.pin11, HLK-PM2.+Vo
  N23: M1.pin12, M2.pin12, HLK-PM2.-Vo
  N24: M2.pin9, M5.pin_2
  N25: M2.pin10, M5.pin_1
  N26: S3.Pin_3, S3.Pin_4, Bauteil3.C7, R51.Pin_0
  N27: S10.Pin_3, S10.Pin_4, Bauteil3.C10, R47.Pin_0
  N28: S11.Pin_3, S11.Pin_4, Bauteil3.C11, R46.Pin_0
  N29: S12.Pin_3, S12.Pin_4, Bauteil3.C12, R45.Pin_0
  N30: S13.Pin_3, S13.Pin_4, Bauteil3.C13, R44.Pin_0
  N31: S14.Pin_3, S14.Pin_4, Bauteil3.C3, R55.Pin_0
  N32: S15.Pin_3, S15.Pin_4, Bauteil3.C2, R56.Pin_0
  N33: S16.Pin_3, S16.Pin_4, Bauteil3.C14, R43.Pin_0
  N34: S17.Pin_3, S17.Pin_4, Bauteil3.C9, R48.Pin_0
  N35: S18.Pin_3, S18.Pin_4, Bauteil3.C0, R58.Pin_0
  N36: S25.G, Bauteil4.C2, R61.Pin_0
  N37: S26.G, Bauteil4.C0, R59.Pin_0
  N38: S27.G, Bauteil4.C3, R62.Pin_0
  N39: S28.G, Bauteil4.C1, R60.Pin_0
  N40: S29.Pin_3, S29.Pin_4, Bauteil3.C4, R54.Pin_0
  N41: S30.Pin_3, S30.Pin_4, Bauteil3.C5, R53.Pin_0
  N42: S31.Pin_3, S31.Pin_4, Bauteil3.C15, R42.Pin_0
  N43: S32.Pin_3, S32.Pin_4, Bauteil3.C6, R52.Pin_0
  N44: S33.Pin_3, S33.Pin_4, Bauteil3.C1, R57.Pin_0
  N45: S34.Pin_3, S34.Pin_4, Bauteil3.C8, R49.Pin_0
  N46: S35.Pin_3, S35.Pin_4, Bauteil4.C4, R50.Pin_0
  N47: Bauteil4.C5, R29.wiper
  N48: Bauteil4.C6, R33.wiper
  N49: Bauteil4.C7, R30.wiper
  N50: Bauteil4.C8, R34.wiper
  N51: Bauteil4.C9, R32.wiper
  N52: Bauteil4.C10, R31.wiper
  N53: U1.Q1, LCD2004-I2C1.RS
  N54: U1.Q2, LCD2004-I2C1.E
  N55: U1.Q3, LCD2004-I2C1.DB4
  N56: U1.Q4, LCD2004-I2C1.DB5
  N57: U1.Q5, LCD2004-I2C1.DB6
  N58: U1.Q6, LCD2004-I2C1.DB7
  N59: LCD2004-I2C1.VDD, LCD2004-I2C1.R/W
  N60: LCD2004-I2C1.V0, R63.wiper
  N61: LCD2004-I2C1.LED+, R64.wiper

notes:
  Pitch
  Roll
  24V Power Supply
  BTS7960
  775 Motor DC 12V-36V 3500-9000Rpm
  CadetYoke v2.0
  from Thingiverse
  5 Way up (left hand)
  5 Way left (left hand)
  5 Way right (left hand)
  5 Way down  (left hand)
  5 Way press (left hand)
  left top (left hand)
  right top (left hand)
  bottom (left hand)
  trim left (left hand)
  trim right (left hand)
  big red (right hand)
  trim down (right hand)
  trim up (right hand)
  right top (right hand)
  left top (right hand)
  bottom (right hand)
  Endswitch Pitch Up
  Endswitch Pitch Down
  Endswitch Roll Down
  Endswitch Roll Up
  Calibration Button
  Roll PWM min
  Roll PWMmax
  Roll Force max
  Pitch PWM min
  Pitch PWM max
  Pitch Force max
  Display 20x4

custom parts:
  BTS7960: BTS7960 43A Peak Power H-Bridge PWM Motor Driver
  Limit Switch: Generic limit switch commonly found on 3D printers. Typical lever microswitch mounted on a PCB board with a 3 pin JST XH connector.
