# Fritzing sketch FFB_Arduino_Yoke_1.1_Micro (saved by Fritzing 0.9.3b)

parts:
  Roll_Driver = BTS7960
  Pitch_Driver = BTS7960
  S3 = Pushbutton [package="[SMD]"]
  Roll_Motor = DC Motor
  Pitch_Motor = DC Motor
  24V_Power_Supply_(example) = HLK-PM12
  S10 = Pushbutton [package="[SMD]"]
  S11 = Pushbutton [package="[SMD]"]
  S12 = Pushbutton [package="[SMD]"]
  S13 = Pushbutton [package="[SMD]"]
  S14 = Pushbutton [package="[SMD]"]
  S15 = Pushbutton [package="[SMD]"]
  S16 = Pushbutton [package="[SMD]"]
  S17 = Pushbutton [package="[SMD]"]
  S18 = Pushbutton [package="[SMD]"]
  R_LEFT = Limit Switch [package="Breakout Board"]
  P_DOWN = Limit Switch [package="Breakout Board"]
  R_RIGHT = Limit Switch [package="Breakout Board"]
  P_UP = Limit Switch [package="Breakout Board"]
  S29 = Pushbutton [package="[SMD]"]
  S30 = Pushbutton [package="[SMD]"]
  S31 = Pushbutton [package="[SMD]"]
  S32 = Pushbutton [package="[SMD]"]
  S33 = Pushbutton [package="[SMD]"]
  S34 = Pushbutton [package="[SMD]"]
  CALIBR = Pushbutton [package="[SMD]"]
  74HC4067_(inside_Yoke) = Analog Digital MUX Breakout
  74HC4067 = Analog Digital MUX Breakout
  P_FORCE = Rotary Potentiometer (Small) [maximum_resistance=10kΩ package=THT]
  P_MIN = Rotary Potentiometer (Small) [maximum_resistance=10kΩ package=THT]
  R_MIN = Rotary Potentiometer (Small) [maximum_resistance=10kΩ package=THT]
  R_MAX = Rotary Potentiometer (Small) [maximum_resistance=10kΩ package=THT]
  P_MAX = Rotary Potentiometer (Small) [maximum_resistance=10kΩ package=THT]
  R_FORCE = Rotary Potentiometer (Small) [maximum_resistance=10kΩ package=THT]
  R42 = Resistor [tolerance=±5% resistance=10k package="0402 [SMD]"]
  R43 = Resistor [tolerance=±5% resistance=10k package="0402 [SMD]"]
  R44 = Resistor [tolerance=±5% resistance=10k package="0402 [SMD]"]
  R45 = Resistor [tolerance=±5% resistance=10k package="0402 [SMD]"]
  R46 = Resistor [tolerance=±5% resistance=10k package="0402 [SMD]"]
  R47 = Resistor [tolerance=±5% resistance=10k package="0402 [SMD]"]
  R48 = Resistor [tolerance=±5% resistance=10k package="0402 [SMD]"]
  R49 = Resistor [tolerance=±5% resistance=10k package="0402 [SMD]"]
  10K-5 = Resistor [tolerance=±5% resistance=10k package="0402 [SMD]"]
  R51 = Resistor [tolerance=±5% resistance=10k package="0402 [SMD]"]
  R52 = Resistor [tolerance=±5% resistance=10k package="0402 [SMD]"]
  R53 = Resistor [tolerance=±5% resistance=10k package="0402 [SMD]"]
  R54 = Resistor [tolerance=±5% resistance=10k package="0402 [SMD]"]
  R55 = Resistor [tolerance=±5% resistance=10k package="0402 [SMD]"]
  R56 = Resistor [tolerance=±5% resistance=10k package="0402 [SMD]"]
  R57 = Resistor [tolerance=±5% resistance=10k package="0402 [SMD]"]
  R58 = Resistor [tolerance=±5% resistance=10k package="0402 [SMD]"]
  10K-4 = Resistor [tolerance=±5% resistance=10k package="0402 [SMD]"]
  10K-3 = Resistor [tolerance=±5% resistance=10k package="0402 [SMD]"]
  10K-2 = Resistor [tolerance=±5% resistance=10k package="0402 [SMD]"]
  10K-1 = Resistor [tolerance=±5% resistance=10k package="0402 [SMD]"]
  CONTRAST = Rotary Potentiometer (Small) [maximum_resistance=10kΩ package=THT]
  LCD_20x4_2004A_V1_1 = 20x4 LCD display [part_number=2004A]
  Arduino_Micro = Arduino Micro (Rev3)
  0_1UF-2 = Ceramic Capacitor [capacitance=0.1µF voltage=10V package="200 mil [THT, multilayer]"]
  0_1UF-1 = Ceramic Capacitor [capacitance=0.1µF voltage=10V package="200 mil [THT, multilayer]"]
  POTI-PITCH = Rotary Potentiometer (Large) [maximum_resistance=100kΩ package=THT]
  POTI-ROLL = Rotary Potentiometer (Large) [maximum_resistance=100kΩ package=THT]

nets:
  N1: Roll_Driver.pin1, Arduino_Micro.D9_PWM/A9
  N2: Roll_Driver.pin2, Arduino_Micro.D10_PWM/A10
  N3: Roll_Driver.pin3, Roll_Driver.pin4, Arduino_Micro.D8_PWM/A8
  VCC: Roll_Driver.pin7, Pitch_Driver.pin7, S3.Pin_1, S3.Pin_2, S10.Pin_1, S10.Pin_2, S11.Pin_1, S11.Pin_2, S12.Pin_1, S12.Pin_2, S13.Pin_1, S13.Pin_2, S14.Pin_1, S14.Pin_2, S15.Pin_1, S15.Pin_2, S16.Pin_1, S16.Pin_2, S17.Pin_1, S17.Pin_2, S18.Pin_1, S18.Pin_2, R_LEFT.S, P_DOWN.S, R_RIGHT.S, P_UP.S, S29.Pin_1, S29.Pin_2, S30.Pin_1, S30.Pin_2, S31.Pin_1, S31.Pin_2, S32.Pin_1, S32.Pin_2, S33.Pin_1, S33.Pin_2, S34.Pin_1, S34.Pin_2, CALIBR.Pin_1, CALIBR.Pin_2, 74HC4067_(inside_Yoke).VCC, 74HC4067.VCC, P_FORCE.leg2, P_MIN.leg2, R_MIN.leg2, R_MAX.leg2, P_MAX.leg2, R_FORCE.leg2, Arduino_Micro.5V, POTI-PITCH.leg1, POTI-ROLL.leg1
  N4: Roll_Driver.pin8, Pitch_Driver.pin8, Arduino_Micro.GND, 0_1UF-2.0, 0_1UF-1.0, POTI-PITCH.leg2, POTI-ROLL.leg2
  N5: Roll_Driver.pin9, Roll_Motor.pin_2
  N6: Roll_Driver.pin10, Roll_Motor.pin_1
  N7: Roll_Driver.pin11, Pitch_Driver.pin11, 24V_Power_Supply_(example).+Vo
  N8: Roll_Driver.pin12, Pitch_Driver.pin12, 24V_Power_Supply_(example).-Vo
  N9: Pitch_Driver.pin1, Arduino_Micro.D6_PWM/A7
  N10: Pitch_Driver.pin2, Arduino_Micro.D13_PWM
  N11: Pitch_Driver.pin3, Pitch_Driver.pin4, Arduino_Micro.D11_PWM
  N12: Pitch_Driver.pin9, Pitch_Motor.pin_2
  N13: Pitch_Driver.pin10, Pitch_Motor.pin_1
  N14: S3.Pin_3, S3.Pin_4, 74HC4067_(inside_Yoke).C7, R51.Pin_0
  N15: S10.Pin_3, S10.Pin_4, 74HC4067_(inside_Yoke).C10, R47.Pin_0
  N16: S11.Pin_3, S11.Pin_4, 74HC4067_(inside_Yoke).C11, R46.Pin_0
  N17: S12.Pin_3, S12.Pin_4, 74HC4067_(inside_Yoke).C12, R45.Pin_0
  N18: S13.Pin_3, S13.Pin_4, 74HC4067_(inside_Yoke).C13, R44.Pin_0
  N19: S14.Pin_3, S14.Pin_4, 74HC4067_(inside_Yoke).C3, R55.Pin_0
  N20: S15.Pin_3, S15.Pin_4, 74HC4067_(inside_Yoke).C2, R56.Pin_0
  N21: S16.Pin_3, S16.Pin_4, 74HC4067_(inside_Yoke).C14, R43.Pin_0
  N22: S17.Pin_3, S17.Pin_4, 74HC4067_(inside_Yoke).C9, R48.Pin_0
  N23: S18.Pin_3, S18.Pin_4, 74HC4067_(inside_Yoke).C0, R58.Pin_0
  N24: R_LEFT.G, 74HC4067.C2, 10K-2.Pin_0
  N25: P_DOWN.G, 74HC4067.C0, 10K-4.Pin_0
  N26: R_RIGHT.G, 74HC4067.C3, 10K-1.Pin_0
  N27: P_UP.G, 74HC4067.C1, 10K-3.Pin_0
  N28: S29.Pin_3, S29.Pin_4, 74HC4067_(inside_Yoke).C4, R54.Pin_0
  N29: S30.Pin_3, S30.Pin_4, 74HC4067_(inside_Yoke).C5, R53.Pin_0
  N30: S31.Pin_3, S31.Pin_4, 74HC4067_(inside_Yoke).C15, R42.Pin_0
  N31: S32.Pin_3, S32.Pin_4, 74HC4067_(inside_Yoke).C6, R52.Pin_0
  N32: S33.Pin_3, S33.Pin_4, 74HC4067_(inside_Yoke).C1, R57.Pin_0
  N33: S34.Pin_3, S34.Pin_4, 74HC4067_(inside_Yoke).C8, R49.Pin_0
  N34: CALIBR.Pin_3, CALIBR.Pin_4, 74HC4067.C4, 10K-5.Pin_0
  GND: 74HC4067_(inside_Yoke).GND, 74HC4067.GND, P_FORCE.leg1, P_MIN.leg1, R_MIN.leg1, R_MAX.leg1, P_MAX.leg1, R_FORCE.leg1, R42.Pin_1, R43.Pin_1, R44.Pin_1, R45.Pin_1, R46.Pin_1, R47.Pin_1, R48.Pin_1, R49.Pin_1, 10K-5.Pin_1, R51.Pin_1, R52.Pin_1, R53.Pin_1, R54.Pin_1, R55.Pin_1, R56.Pin_1, R57.Pin_1, R58.Pin_1, 10K-4.Pin_1, 10K-3.Pin_1, 10K-2.Pin_1, 10K-1.Pin_1, CONTRAST.leg2, LCD_20x4_2004A_V1_1.Vss, LCD_20x4_2004A_V1_1.R/W, LCD_20x4_2004A_V1_1.DB0, LCD_20x4_2004A_V1_1.DB1, LCD_20x4_2004A_V1_1.DB2, LCD_20x4_2004A_V1_1.DB3, LCD_20x4_2004A_V1_1.K_-
  N35: 74HC4067_(inside_Yoke).EN, Arduino_Micro.D2/SDA
  N36: 74HC4067_(inside_Yoke).S0, 74HC4067.S0, LCD_20x4_2004A_V1_1.DB4, Arduino_Micro.D4_PWM/A6
  N37: 74HC4067_(inside_Yoke).S1, 74HC4067.S1, LCD_20x4_2004A_V1_1.DB5, Arduino_Micro.D5_PWM
  N38: 74HC4067_(inside_Yoke).S2, 74HC4067.S2, LCD_20x4_2004A_V1_1.DB6, Arduino_Micro.D3/SCL
  N39: 74HC4067_(inside_Yoke).S3, 74HC4067.S3, LCD_20x4_2004A_V1_1.DB7, Arduino_Micro.D7
  N40: 74HC4067_(inside_Yoke).SIG, Arduino_Micro.A5
  N41: 74HC4067.C5, P_FORCE.wiper
  N42: 74HC4067.C6, P_MAX.wiper
  N43: 74HC4067.C7, P_MIN.wiper
  N44: 74HC4067.C8, R_FORCE.wiper
  N45: 74HC4067.C9, R_MAX.wiper
  N46: 74HC4067.C10, R_MIN.wiper
  N47: 74HC4067.EN, Arduino_Micro.D1/TX
  N48: 74HC4067.SIG, Arduino_Micro.A4
  N49: CONTRAST.leg1, LCD_20x4_2004A_V1_1.Vdd, LCD_20x4_2004A_V1_1.A_+
  N50: CONTRAST.wiper, LCD_20x4_2004A_V1_1.Vo
  N51: LCD_20x4_2004A_V1_1.RS, Arduino_Micro.D12_PWM/A11
  N52: LCD_20x4_2004A_V1_1.E, Arduino_Micro.D0/RX
  N53: Arduino_Micro.A1, 0_1UF-1.1, POTI-PITCH.wiper
  N54: Arduino_Micro.A0, 0_1UF-2.1, POTI-ROLL.wiper

notes:
  Pitch
  Roll
  24V Power Supply
  BTS7960
  775 Motor DC 12V-36V 3500-9000Rpm
  inside CadetYoke v2.0
  from Thingiverse
  5 Way up (left hand)
  5 Way left (left hand)
  5 Way right (left hand)
  5 Way down  (left hand)
  5 Way press (left hand)
  left top (left hand)
  right top (left hand)
  bottom (left hand)
  trim left (left hand)
  trim right (left hand)
  big red (right hand)
  trim down (right hand)
  trim up (right hand)
  right top (right hand)
  left top (right hand)
  bottom (right hand)
  Endswitch Pitch Up
  Endswitch Pitch Down
  Endswitch Roll Down
  Endswitch Roll Up
  Calibration Button
  Roll PWM min
  Roll PWMmax
  Roll Force max
  Pitch PWM min
  Pitch PWM max
  Pitch Force max
  CONTRAST
  20x4 LCD Display 2004A v1.1

custom parts:
  BTS7960: BTS7960 43A Peak Power H-Bridge PWM Motor Driver
  Limit Switch: Generic limit switch commonly found on 3D printers. Typical lever microswitch mounted on a PCB board with a 3 pin JST XH connector.
  20x4 LCD display: 20x4 character display. CHECK LED POLARITY BEFORE CONNECTING POWER Some versions of the dispaly have the polarity of the LED pins "A" and "K" reversed.
